// Logisim project catraca.circ as structural Verilog: 4 circuits, main circuit main
module main (
);

  wire and_1_out, button_1_out, contador_1_out_3, contador_1_out_4, contador_1_out_5, contador_1_out_6,
       contador_1_out_7, contador_1_out_8, contador_1_out_9, contador_1_out_10, contador_2_out_3,
       contador_2_out_4, contador_2_out_5, contador_2_out_6, contador_2_out_7, contador_2_out_8,
       contador_2_out_9, contador_2_out_10, contador_3_out_3, contador_3_out_4, contador_3_out_5,
       contador_3_out_6, contador_3_out_7, contador_3_out_8, contador_3_out_9, contador_3_out_10,
       contador_4_out_3, contador_4_out_4, contador_4_out_5, contador_4_out_6, contador_4_out_7,
       contador_4_out_8, contador_4_out_9, contador_4_out_10, controlled_inverter_1_out, d_ff_1_q,
       lubrificar_1_out_2;

  Contador contador_1 (
    .in_1(contador_2_out_10), .in_2(lubrificar_1_out_2), .out_3(contador_1_out_3), .out_4(contador_1_out_4),
    .out_5(contador_1_out_5), .out_6(contador_1_out_6), .out_7(contador_1_out_7), .out_8(contador_1_out_8),
    .out_9(contador_1_out_9), .out_10(contador_1_out_10));
  _7_Segment_Display u_7_segment_display_1 (
    .g(contador_1_out_9), .f(contador_1_out_8), .a(contador_1_out_3), .b(contador_1_out_4),
    .e(contador_1_out_7), .d(contador_1_out_6), .c(contador_1_out_5));  // open: dp
  D_Flip_Flop d_ff_1 (
    .clk(contador_1_out_10), .D(contador_1_out_10), .Q(d_ff_1_q), .reset(lubrificar_1_out_2));  // open: Qn, preset, en
  Contador contador_2 (
    .in_1(contador_3_out_10), .in_2(lubrificar_1_out_2), .out_3(contador_2_out_3), .out_4(contador_2_out_4),
    .out_5(contador_2_out_5), .out_6(contador_2_out_6), .out_7(contador_2_out_7), .out_8(contador_2_out_8),
    .out_9(contador_2_out_9), .out_10(contador_2_out_10));
  _7_Segment_Display u_7_segment_display_2 (
    .g(contador_2_out_9), .f(contador_2_out_8), .a(contador_2_out_3), .b(contador_2_out_4),
    .e(contador_2_out_7), .d(contador_2_out_6), .c(contador_2_out_5));  // open: dp
  Contador contador_3 (
    .in_1(contador_4_out_10), .in_2(lubrificar_1_out_2), .out_3(contador_3_out_3), .out_4(contador_3_out_4),
    .out_5(contador_3_out_5), .out_6(contador_3_out_6), .out_7(contador_3_out_7), .out_8(contador_3_out_8),
    .out_9(contador_3_out_9), .out_10(contador_3_out_10));
  _7_Segment_Display u_7_segment_display_3 (
    .g(contador_3_out_9), .f(contador_3_out_8), .a(contador_3_out_3), .b(contador_3_out_4),
    .e(contador_3_out_7), .d(contador_3_out_6), .c(contador_3_out_5));  // open: dp
  Contador contador_4 (
    .in_1(and_1_out), .in_2(lubrificar_1_out_2), .out_3(contador_4_out_3), .out_4(contador_4_out_4),
    .out_5(contador_4_out_5), .out_6(contador_4_out_6), .out_7(contador_4_out_7), .out_8(contador_4_out_8),
    .out_9(contador_4_out_9), .out_10(contador_4_out_10));
  _7_Segment_Display u_7_segment_display_4 (
    .g(contador_4_out_9), .f(contador_4_out_8), .a(contador_4_out_3), .b(contador_4_out_4),
    .e(contador_4_out_7), .d(contador_4_out_6), .c(contador_4_out_5));  // open: dp
  and and_1 (and_1_out, button_1_out, controlled_inverter_1_out);
  LUBRIFICAR lubrificar_1 (.in_1(d_ff_1_q), .out_2(lubrificar_1_out_2));
  assign controlled_inverter_1_out = 1'b1 ? ~d_ff_1_q : 1'bz;  // Controlled_Inverter controlled_inverter_1
  Counter counter_1 (.clk(lubrificar_1_out_2));  // open: load, D, count, Q, carry, clr
  Button button_1 (.out(button_1_out));

  // Notes on the sheet:
  //   LUBRIFICAR
  //   CONTA O NUMERO DE LUBRIFICAÇÕES
  //   PASSAGEIRO
endmodule

module tradutor0ate9 (
  input  A,
  input  B,
  input  C,
  input  D,
  output a_2,
  output b_2,
  output c_2,
  output d_2,
  output e,
  output f,
  output g
);

  wire and_1_out, and_2_out, and_3_out, and_4_out, and_5_out, and_6_out, and_7_out, and_8_out, and_9_out,
       and_10_out, and_11_out, and_12_out, and_13_out, and_14_out, and_15_out, and_16_out, and_17_out,
       and_18_out, and_19_out, and_20_out, not_1_out, not_2_out, not_3_out, not_4_out, not_5_out, not_6_out,
       not_7_out, not_8_out, not_9_out, not_10_out, not_11_out, not_12_out, not_13_out, not_14_out,
       not_15_out, not_16_out, not_17_out, not_18_out, not_19_out, not_20_out, not_21_out, not_22_out,
       or_1_out, or_2_out, or_3_out, or_4_out, or_6_out, or_7_out, or_8_out, or_9_out, or_10_out, or_13_out,
       or_14_out;

  not not_1 (not_1_out, B);
  and and_1 (and_1_out, not_1_out, not_2_out);
  not not_2 (not_2_out, D);
  and and_2 (and_2_out, B, D);
  not not_3 (not_3_out, B);
  not not_4 (not_4_out, C);
  and and_3 (and_3_out, not_4_out, not_5_out);
  not not_5 (not_5_out, D);
  not not_6 (not_6_out, C);
  or or_1 (or_1_out, not_6_out, D);
  not not_7 (not_7_out, B);
  not not_8 (not_8_out, D);
  not not_9 (not_9_out, B);
  not not_10 (not_10_out, D);
  and and_4 (and_4_out, B, not_11_out);
  not not_11 (not_11_out, C);
  not not_12 (not_12_out, B);
  and and_5 (and_5_out, not_12_out, not_13_out);
  not not_13 (not_13_out, D);
  and and_6 (and_6_out, C, not_14_out);
  not not_14 (not_14_out, D);
  and and_7 (and_7_out, A, B);
  not not_15 (not_15_out, C);
  and and_8 (and_8_out, not_15_out, D);
  not not_16 (not_16_out, C);
  and and_9 (and_9_out, not_16_out, not_17_out);
  not not_17 (not_17_out, D);
  and and_10 (and_10_out, B, not_18_out);
  not not_18 (not_18_out, C);
  and and_11 (and_11_out, B, not_19_out);
  not not_19 (not_19_out, D);
  not not_20 (not_20_out, B);
  and and_12 (and_12_out, not_20_out, C);
  and and_13 (and_13_out, B, not_21_out);
  not not_21 (not_21_out, C);
  and and_14 (and_14_out, B, not_22_out);
  not not_22 (not_22_out, D);
  or or_2 (or_2_out, and_1_out, C);
  or or_3 (or_3_out, and_2_out, A);
  or or_4 (or_4_out, not_3_out, and_3_out);
  and and_15 (and_15_out, C, D);
  or or_5 (c_2, or_1_out, B);
  and and_16 (and_16_out, not_7_out, not_8_out);
  and and_17 (and_17_out, not_9_out, C);
  and and_18 (and_18_out, C, not_10_out);
  and and_19 (and_19_out, and_4_out, D);
  or or_6 (or_6_out, and_5_out, and_6_out);
  and and_20 (and_20_out, and_7_out, and_8_out);
  or or_7 (or_7_out, and_9_out, and_10_out);
  or or_8 (or_8_out, and_11_out, A);
  or or_9 (or_9_out, and_12_out, and_13_out);
  or or_10 (or_10_out, and_14_out, A);
  or or_11 (a_2, or_2_out, or_3_out);
  or or_12 (b_2, or_4_out, and_15_out);
  or or_13 (or_13_out, and_16_out, and_17_out);
  or or_14 (or_14_out, and_18_out, and_19_out);
  or or_15 (e, or_6_out, and_20_out);
  or or_16 (f, or_7_out, or_8_out);
  or or_17 (g, or_9_out, or_10_out);
  or or_18 (d_2, or_13_out, or_14_out);
endmodule

module Contador (
  input  in_1,
  input  in_2,
  output out_3,
  output out_4,
  output out_5,
  output out_6,
  output out_7,
  output out_8,
  output out_9,
  output out_10
);

  wire and_2_out, j_k_ff_1_q, j_k_ff_1_qn, j_k_ff_2_q, j_k_ff_2_qn, j_k_ff_3_q, j_k_ff_3_qn, j_k_ff_4_q,
       or_1_out;

  J_K_Flip_Flop j_k_ff_1 (
    .J(1'b1), .clk(in_1), .K(1'b1), .Q(j_k_ff_1_q), .Qn(j_k_ff_1_qn), .en(1'b1), .reset(or_1_out));  // open: preset
  or or_1 (or_1_out, in_2, and_2_out);
  and and_1 (out_10, ~in_2, and_2_out);  // AND_Gate
  and and_2 (and_2_out, j_k_ff_4_q, j_k_ff_2_q);
  J_K_Flip_Flop j_k_ff_2 (
    .J(1'b1), .clk(j_k_ff_1_qn), .K(1'b1), .Q(j_k_ff_2_q), .Qn(j_k_ff_2_qn), .en(1'b1), .reset(or_1_out));  // open: preset
  J_K_Flip_Flop j_k_ff_3 (
    .J(1'b1), .clk(j_k_ff_2_qn), .K(1'b1), .Q(j_k_ff_3_q), .Qn(j_k_ff_3_qn), .en(1'b1), .reset(or_1_out));  // open: preset
  J_K_Flip_Flop j_k_ff_4 (
    .J(1'b1), .clk(j_k_ff_3_qn), .K(1'b1), .Q(j_k_ff_4_q), .en(1'b1), .reset(or_1_out));  // open: Qn, preset
  tradutor0ate9 tradutor0ate9_1 (
    .A(j_k_ff_4_q), .B(j_k_ff_3_q), .C(j_k_ff_2_q), .D(j_k_ff_1_q), .a_2(out_3), .b_2(out_4), .c_2(out_5),
    .d_2(out_6), .e(out_7), .f(out_8), .g(out_9));
endmodule

module LUBRIFICAR (
  input  in_1,
  output out_2
);


  assign out_2 = in_1;
endmodule
