// Logisim project circuitos.circ as structural Verilog: 3 circuits, main circuit SistemaDePostes
module SistemaDePostes (
);

  wire and_1_out, and_2_out, and_3_out, and_4_out, and_5_out, and_6_out, and_7_out, and_8_out, button_1_out,
       clock_1_out, contador1hora_1_out_2, contador15min_1_out_2, contador15min_2_out_2,
       contador15min_3_out_2, contador15min_4_out_2, contador15min_5_out_2, controlled_inverter_1_out,
       d_ff_1_q, d_ff_2_q, d_ff_3_q, d_ff_4_q, d_ff_5_q, d_ff_6_q, d_ff_7_q, d_ff_8_q, d_ff_9_q, d_ff_10_q,
       d_ff_11_q, d_ff_12_q, d_ff_13_q, j_k_ff_1_qn, j_k_ff_2_qn, j_k_ff_3_q, j_k_ff_3_qn, j_k_ff_4_q;

  Button button_1 (.out(button_1_out));
  Clock clock_1 (.out(clock_1_out));
  D_Flip_Flop d_ff_1 (
    .clk(button_1_out), .D(button_1_out), .Q(d_ff_1_q), .en(button_1_out), .reset(d_ff_13_q));  // open: Qn, preset
  D_Flip_Flop d_ff_2 (.clk(and_1_out), .D(and_1_out), .Q(d_ff_2_q), .reset(d_ff_13_q));  // open: Qn, preset, en
  LED led_1 (.in(d_ff_2_q));
  LED led_2 (.in(d_ff_3_q));
  D_Flip_Flop d_ff_3 (.clk(and_2_out), .D(and_2_out), .Q(d_ff_3_q), .reset(d_ff_13_q));  // open: Qn, preset, en
  LED led_3 (.in(d_ff_4_q));
  D_Flip_Flop d_ff_4 (.clk(and_3_out), .D(and_3_out), .Q(d_ff_4_q), .reset(d_ff_13_q));  // open: Qn, preset, en
  D_Flip_Flop d_ff_5 (.clk(and_4_out), .D(and_4_out), .Q(d_ff_5_q), .reset(d_ff_13_q));  // open: Qn, preset, en
  LED led_4 (.in(d_ff_5_q));
  LED led_5 (.in(d_ff_6_q));
  D_Flip_Flop d_ff_6 (.clk(and_5_out), .D(and_5_out), .Q(d_ff_6_q), .reset(d_ff_13_q));  // open: Qn, preset, en
  D_Flip_Flop d_ff_7 (.clk(and_6_out), .D(and_6_out), .Q(d_ff_7_q), .reset(d_ff_13_q));  // open: Qn, preset, en
  LED led_6 (.in(d_ff_7_q));
  and and_1 (and_1_out, d_ff_1_q, clock_1_out);
  contador15min contador15min_1 (.in_1(and_1_out), .out_2(contador15min_1_out_2));
  contador15min contador15min_2 (.in_1(and_2_out), .out_2(contador15min_2_out_2));
  contador15min contador15min_3 (.in_1(and_3_out), .out_2(contador15min_3_out_2));
  contador15min contador15min_4 (.in_1(and_4_out), .out_2(contador15min_4_out_2));
  contador15min contador15min_5 (.in_1(and_5_out), .out_2(contador15min_5_out_2));
  D_Flip_Flop d_ff_8 (
    .clk(contador15min_1_out_2), .D(contador15min_1_out_2), .Q(d_ff_8_q), .reset(d_ff_13_q));  // open: Qn, preset, en
  D_Flip_Flop d_ff_9 (
    .clk(contador15min_2_out_2), .D(contador15min_2_out_2), .Q(d_ff_9_q), .reset(d_ff_13_q));  // open: Qn, preset, en
  D_Flip_Flop d_ff_10 (
    .clk(contador15min_3_out_2), .D(contador15min_3_out_2), .Q(d_ff_10_q), .reset(d_ff_13_q));  // open: Qn, preset, en
  D_Flip_Flop d_ff_11 (
    .clk(contador15min_4_out_2), .D(contador15min_4_out_2), .Q(d_ff_11_q), .reset(d_ff_13_q));  // open: Qn, preset, en
  D_Flip_Flop d_ff_12 (
    .clk(contador15min_5_out_2), .D(contador15min_5_out_2), .Q(d_ff_12_q), .reset(d_ff_13_q));  // open: Qn, preset, en
  contador1hora contador1hora_1 (.in_1(and_6_out), .out_2(contador1hora_1_out_2));
  J_K_Flip_Flop j_k_ff_1 (
    .J(1'b1), .clk(contador1hora_1_out_2), .K(1'b1), .Qn(j_k_ff_1_qn), .en(1'b1), .reset(and_8_out));  // open: Q, preset
  and and_2 (and_2_out, clock_1_out, d_ff_8_q);
  and and_3 (and_3_out, clock_1_out, d_ff_9_q);
  and and_4 (and_4_out, clock_1_out, d_ff_10_q);
  and and_5 (and_5_out, clock_1_out, d_ff_11_q);
  and and_6 (and_6_out, clock_1_out, d_ff_12_q);
  J_K_Flip_Flop j_k_ff_2 (
    .J(1'b1), .clk(j_k_ff_1_qn), .K(1'b1), .Qn(j_k_ff_2_qn), .en(1'b1), .reset(and_8_out));  // open: Q, preset
  assign controlled_inverter_1_out = 1'b1 ? ~d_ff_12_q : 1'bz;  // Controlled_Inverter controlled_inverter_1
  J_K_Flip_Flop j_k_ff_3 (
    .J(1'b1), .clk(j_k_ff_2_qn), .K(1'b1), .Q(j_k_ff_3_q), .Qn(j_k_ff_3_qn), .en(1'b1), .reset(and_8_out));  // open: preset
  D_Flip_Flop d_ff_13 (.clk(and_8_out), .D(and_8_out), .Q(d_ff_13_q), .reset(and_7_out));  // open: Qn, preset, en
  and and_7 (and_7_out, d_ff_13_q, controlled_inverter_1_out);
  and and_8 (and_8_out, j_k_ff_3_q, j_k_ff_4_q);
  J_K_Flip_Flop j_k_ff_4 (
    .J(1'b1), .clk(j_k_ff_3_qn), .K(1'b1), .Q(j_k_ff_4_q), .en(1'b1), .reset(and_8_out));  // open: Qn, preset

  // Notes on the sheet:
  //   ZONA A
  //   ZONA B
  //   ZONA C
  //   ZONA D
  //   ZONA E
  //   ZONA F
endmodule

module contador15min (
  input  in_1,
  output out_2
);

  wire and_1_out, and_2_out, j_k_ff_1_qn, j_k_ff_2_q, j_k_ff_2_qn, j_k_ff_3_qn, j_k_ff_4_q, j_k_ff_5_qn,
       j_k_ff_6_q, j_k_ff_6_qn, j_k_ff_7_q, j_k_ff_7_qn, j_k_ff_8_q, j_k_ff_8_qn, j_k_ff_9_q, j_k_ff_10_q,
       j_k_ff_10_qn, j_k_ff_11_q;

  J_K_Flip_Flop j_k_ff_1 (
    .J(1'b1), .clk(in_1), .K(1'b1), .Qn(j_k_ff_1_qn), .en(1'b1), .reset(and_1_out));  // open: Q, preset
  J_K_Flip_Flop j_k_ff_2 (
    .J(1'b1), .clk(j_k_ff_1_qn), .K(1'b1), .Q(j_k_ff_2_q), .Qn(j_k_ff_2_qn), .en(1'b1), .reset(and_1_out));  // open: preset
  J_K_Flip_Flop j_k_ff_3 (
    .J(1'b1), .clk(j_k_ff_2_qn), .K(1'b1), .Qn(j_k_ff_3_qn), .en(1'b1), .reset(and_1_out));  // open: Q, preset
  and and_1 (and_1_out, j_k_ff_4_q, j_k_ff_2_q);
  J_K_Flip_Flop j_k_ff_4 (
    .J(1'b1), .clk(j_k_ff_3_qn), .K(1'b1), .Q(j_k_ff_4_q), .en(1'b1), .reset(and_1_out));  // open: Qn, preset
  J_K_Flip_Flop j_k_ff_5 (
    .J(1'b1), .clk(and_1_out), .K(1'b1), .Qn(j_k_ff_5_qn), .en(1'b1), .reset(and_2_out));  // open: Q, preset
  J_K_Flip_Flop j_k_ff_6 (
    .J(1'b1), .clk(and_2_out), .K(1'b1), .Q(j_k_ff_6_q), .Qn(j_k_ff_6_qn), .en(1'b1), .reset(out_2));  // open: preset
  J_K_Flip_Flop j_k_ff_7 (
    .J(1'b1), .clk(j_k_ff_5_qn), .K(1'b1), .Q(j_k_ff_7_q), .Qn(j_k_ff_7_qn), .en(1'b1), .reset(and_2_out));  // open: preset
  J_K_Flip_Flop j_k_ff_8 (
    .J(1'b1), .clk(j_k_ff_6_qn), .K(1'b1), .Q(j_k_ff_8_q), .Qn(j_k_ff_8_qn), .en(1'b1), .reset(out_2));  // open: preset
  J_K_Flip_Flop j_k_ff_9 (
    .J(1'b1), .clk(j_k_ff_7_qn), .K(1'b1), .Q(j_k_ff_9_q), .en(1'b1), .reset(and_2_out));  // open: Qn, preset
  and and_2 (and_2_out, j_k_ff_7_q, j_k_ff_9_q);
  J_K_Flip_Flop j_k_ff_10 (
    .J(1'b1), .clk(j_k_ff_8_qn), .K(1'b1), .Q(j_k_ff_10_q), .Qn(j_k_ff_10_qn), .en(1'b1), .reset(out_2));  // open: preset
  J_K_Flip_Flop j_k_ff_11 (
    .J(1'b1), .clk(j_k_ff_10_qn), .K(1'b1), .Q(j_k_ff_11_q), .en(1'b1), .reset(out_2));  // open: Qn, preset
  and and_3 (out_2, j_k_ff_6_q, j_k_ff_8_q, j_k_ff_10_q, j_k_ff_11_q);
endmodule

module contador1hora (
  input  in_1,
  output out_2
);

  wire and_1_out, and_2_out, and_3_out, contador15min_1_out_2, contador15min_2_out_2, contador15min_3_out_2,
       d_ff_1_q, d_ff_2_q, d_ff_3_q;

  contador15min contador15min_1 (.in_1(in_1), .out_2(contador15min_1_out_2));
  D_Flip_Flop d_ff_1 (
    .clk(contador15min_1_out_2), .D(contador15min_1_out_2), .Q(d_ff_1_q), .reset(out_2));  // open: Qn, preset, en
  and and_1 (and_1_out, d_ff_1_q, in_1);
  contador15min contador15min_2 (.in_1(and_1_out), .out_2(contador15min_2_out_2));
  D_Flip_Flop d_ff_2 (
    .clk(contador15min_2_out_2), .D(contador15min_2_out_2), .Q(d_ff_2_q), .reset(out_2));  // open: Qn, preset, en
  and and_2 (and_2_out, d_ff_2_q, in_1);
  contador15min contador15min_3 (.in_1(and_2_out), .out_2(contador15min_3_out_2));
  D_Flip_Flop d_ff_3 (
    .clk(contador15min_3_out_2), .D(contador15min_3_out_2), .Q(d_ff_3_q), .reset(out_2));  // open: Qn, preset, en
  and and_3 (and_3_out, d_ff_3_q, in_1);
  contador15min contador15min_4 (.in_1(and_3_out), .out_2(out_2));
endmodule
